# Fritzing sketch RelogioBCD (saved by Fritzing 0.9.6b)
circuit board: 8.46667cm x 5.64444cm

parts:
  U3 = USB connector [package=THT]
  R4 = Resistor [tolerance=±5% resistance=150 power=0.25 package=THT]
  R2 = Resistor [tolerance=±5% resistance=150 power=0.25 package=THT]
  R5 = Resistor [tolerance=±5% resistance=150 power=0.25 package=THT]
  R3 = Resistor [tolerance=±5% resistance=150 power=0.25 package=THT]
  U1 = ESP-12F (ESP8266 WiFi Module) [part_number=ESP8266]
  Disp1 = 60mm 8x8 dot matrix column cathode led display with standard pcb pads
  U4 = LM1117 [part_number=LM1117 package=SOT-223]
  R6 = Resistor [tolerance=±5% resistance=150 power=0.25 package=THT]

nets:
  5V: U3.5V, U4.Vin
  GND: U3.chassis5, U3.chassis6, U1.GND, U4.GND, R6.Pin_1
  N1: R4.Pin_0, Disp1.pin_7
  N2: R4.Pin_1, U1.GPIO15, R6.Pin_0
  N3: R2.Pin_0, U1.TXD0
  N4: R2.Pin_1, Disp1.pin_1
  N5: R5.Pin_0, Disp1.pin_5
  N6: R5.Pin_1, U1.GPIO2
  N7: R3.Pin_0, U1.RXD0
  N8: R3.Pin_1, Disp1.pin_2
  N9: U1.VCC, U1.EN, U4.Vout
  N10: U1.GPIO0, Disp1.pin_6
  N11: U1.GPIO4, Disp1.pin_4
  N12: U1.GPIO5, Disp1.pin_3
  N13: U1.GPIO16, Disp1.pin_16
  N14: U1.GPIO14, Disp1.pin_15
  N15: U1.GPIO12, Disp1.pin_11
  N16: U1.GPIO13, Disp1.pin_10

custom parts:
  ESP-12F (ESP8266 WiFi Module): WiFi Module based on the ESP8266 with onboard PCB antenna and UART communications
  LM1117: Top view SOT-223 package.
